// Logisim project FinalElevator.circ as structural Verilog: 5 circuits, main circuit main
module main (
);

  wire ALARM_OFF_out, ALARM_ON_out, ButtonBrain_alarm_led, ButtonBrain_call0t, ButtonBrain_call1t,
       ButtonBrain_call2t, ButtonBrain_go0t, ButtonBrain_go1t, ButtonBrain_go2t, call_to_1_ff2_q,
       call_to_1_ff_q, CALL_to_1st_out, call_to_2_ff2_q, call_to_2_ff_q, CALL_to_2nd_out,
       CALL_to_ground_2_out, call_to_ground_q, call_to_the_ground_ff2_q, Clock_out, decoder_1_out0,
       decoder_1_out1, decoder_2_out0, decoder_2_out1, ElevatorBrain_busyornot, ElevatorBrain_door,
       ElevatorBrain_down, ElevatorBrain_indicate0, ElevatorBrain_indicate1, ElevatorBrain_indicate2,
       ElevatorBrain_up, First_q, GO_1st_out, Go_2nd_out, go_to_1_ff2_q, go_to_1_ff_q, go_to_2_ff2_q,
       go_to_2_ff_q, go_to_ground_ff2_q, go_to_ground_ff_q, GO_to_ground_out, Ground_q, Indicator_a,
       Indicator_b, Indicator_c, Indicator_d, Indicator_e, Indicator_f, Indicator_g, Indicator_point,
       or_1_out, or_2_out, or_3_out, or_4_out, or_5_out, or_6_out, Second_q;

  or or_1 (or_1_out, call_to_the_ground_ff2_q, call_to_ground_q);
  or or_2 (or_2_out, call_to_2_ff2_q, call_to_2_ff_q);
  or or_3 (or_3_out, go_to_1_ff2_q, go_to_1_ff_q);
  Clock Clock (.out(Clock_out));
  D_Flip_Flop Ground (.clk(Clock_out), .D(ElevatorBrain_indicate0), .Q(Ground_q));  // open: Qn, preset, en, reset
  D_Flip_Flop First (.clk(Clock_out), .D(ElevatorBrain_indicate1), .Q(First_q));  // open: Qn, preset, en, reset
  D_Flip_Flop Second (.clk(Clock_out), .D(ElevatorBrain_indicate2), .Q(Second_q));  // open: Qn, preset, en, reset
  D_Flip_Flop call_to_the_ground_ff2 (
    .clk(Clock_out), .D(call_to_ground_q), .Q(call_to_the_ground_ff2_q));  // open: Qn, preset, en, reset
  D_Flip_Flop call_to_ground (
    .clk(Clock_out), .D(ButtonBrain_call0t), .Q(call_to_ground_q));  // open: Qn, preset, en, reset
  D_Flip_Flop call_to_2_ff2 (.clk(Clock_out), .D(call_to_2_ff_q), .Q(call_to_2_ff2_q));  // open: Qn, preset, en, reset
  D_Flip_Flop call_to_2_ff (
    .clk(Clock_out), .D(ButtonBrain_call2t), .Q(call_to_2_ff_q));  // open: Qn, preset, en, reset
  D_Flip_Flop go_to_1_ff2 (.clk(Clock_out), .D(go_to_1_ff_q), .Q(go_to_1_ff2_q));  // open: Qn, preset, en, reset
  D_Flip_Flop go_to_1_ff (.clk(Clock_out), .D(ButtonBrain_go1t), .Q(go_to_1_ff_q));  // open: Qn, preset, en, reset
  D_Flip_Flop call_to_1_ff2 (.clk(Clock_out), .D(call_to_1_ff_q), .Q(call_to_1_ff2_q));  // open: Qn, preset, en, reset
  or or_4 (or_4_out, call_to_1_ff2_q, call_to_1_ff_q);
  D_Flip_Flop call_to_1_ff (
    .clk(Clock_out), .D(ButtonBrain_call1t), .Q(call_to_1_ff_q));  // open: Qn, preset, en, reset
  D_Flip_Flop go_to_ground_ff2 (
    .clk(Clock_out), .D(go_to_ground_ff_q), .Q(go_to_ground_ff2_q));  // open: Qn, preset, en, reset
  or or_5 (or_5_out, go_to_ground_ff2_q, go_to_ground_ff_q);
  D_Flip_Flop go_to_ground_ff (
    .clk(Clock_out), .D(ButtonBrain_go0t), .Q(go_to_ground_ff_q));  // open: Qn, preset, en, reset
  D_Flip_Flop go_to_2_ff2 (.clk(Clock_out), .D(go_to_2_ff_q), .Q(go_to_2_ff2_q));  // open: Qn, preset, en, reset
  or or_6 (or_6_out, go_to_2_ff2_q, go_to_2_ff2_q, go_to_2_ff_q, go_to_2_ff_q, go_to_2_ff_q);
  D_Flip_Flop go_to_2_ff (.clk(Clock_out), .D(ButtonBrain_go2t), .Q(go_to_2_ff_q));  // open: Qn, preset, en, reset
  elevator ElevatorBrain (
    .GroundRN(Ground_q), .Floor1RN(First_q), .Floor2RN(Second_q), .call_to_0(or_1_out), .call_to_1(or_4_out),
    .call_to_2(or_2_out), .goto_floor(or_5_out), .goto1(or_3_out), .go_to_2(or_6_out),
    .indicate0(ElevatorBrain_indicate0), .indicate1(ElevatorBrain_indicate1),
    .indicate2(ElevatorBrain_indicate2), .BusyorNot(ElevatorBrain_busyornot), .Door(ElevatorBrain_door),
    .up(ElevatorBrain_up), .Down(ElevatorBrain_down));
  Decoder #(.enable("false")) decoder_1 (.out0(decoder_1_out0), .out1(decoder_1_out1), .sel(ElevatorBrain_door));
  Button ALARM_ON (.out(ALARM_ON_out));
  Decoder #(.enable("false")) decoder_2 (.out0(decoder_2_out0), .out1(decoder_2_out1), .sel(ElevatorBrain_busyornot));
  LED ALARM_LED (.in(ButtonBrain_alarm_led));
  indicator Indicator (
    .floor0(ElevatorBrain_indicate0), .floor1(ElevatorBrain_indicate1), .floor_2(ElevatorBrain_indicate2),
    .a(Indicator_a), .b(Indicator_b), .c(Indicator_c), .d(Indicator_d), .e(Indicator_e), .f(Indicator_f),
    .g(Indicator_g), .Point(Indicator_point));
  _7_Segment_Display u_7_segment_display_1 (
    .g(Indicator_g), .f(Indicator_f), .a(Indicator_a), .b(Indicator_b), .e(Indicator_e), .d(Indicator_d),
    .c(Indicator_c), .dp(Indicator_point));
  Button ALARM_OFF (.out(ALARM_OFF_out));
  LED Up (.in(ElevatorBrain_up));
  LED Down (.in(ElevatorBrain_down));
  Button CALL_to_2nd (.out(CALL_to_2nd_out));
  Button CALL_to_1st (.out(CALL_to_1st_out));
  Button CALL_to_ground_2 (.out(CALL_to_ground_2_out));
  LED Door_Closed (.in(decoder_1_out1));
  LED Door_Open (.in(decoder_1_out0));
  LED Busy (.in(decoder_2_out1));
  LED Usable (.in(decoder_2_out0));
  Button Go_2nd (.out(Go_2nd_out));
  Button GO_1st (.out(GO_1st_out));
  Button GO_to_ground (.out(GO_to_ground_out));
  ButtonsWAlarm ButtonBrain (
    .Go2(Go_2nd_out), .Go1(GO_1st_out), .Go0(GO_to_ground_out), .Call2(CALL_to_2nd_out),
    .Call1(CALL_to_1st_out), .Call0(CALL_to_ground_2_out), .Alarm_ON(ALARM_ON_out),
    .Alarm_OFF(ALARM_OFF_out), .go2t(ButtonBrain_go2t), .go1t(ButtonBrain_go1t), .go0t(ButtonBrain_go0t),
    .call2t(ButtonBrain_call2t), .call1t(ButtonBrain_call1t), .call0t(ButtonBrain_call0t),
    .Alarm_LED(ButtonBrain_alarm_led));

  // Notes on the sheet:
  //   Flip Flops that store floor numbers
  //   Counters are placed in order to induce a delay and show the floors moving across, and for example, so that the 1st floor can be seen when going from the 0th floor to the 2nd floor.
  //   Floor Display
  //   Outside 
  //   The initial value was taken as floor 0.
  //   Inside
endmodule

module indicator (
  input  floor0,
  input  floor1,
  input  floor_2,
  output a,
  output b,
  output c,
  output d,
  output e,
  output f,
  output g,
  output Point
);

  wire and_1_out, and_2_out, and_3_out, and_4_out, and_5_out, and_6_out, and_7_out, and_8_out, and_9_out,
       and_10_out, and_11_out, not_1_out, not_2_out, not_3_out, not_4_out, not_5_out, not_6_out, not_7_out,
       not_8_out, not_9_out, not_10_out, not_11_out, not_12_out, not_13_out, not_14_out, not_15_out,
       not_16_out, not_17_out, not_18_out, not_19_out, not_20_out, not_21_out, not_22_out, not_23_out,
       not_24_out, not_25_out, not_26_out;

  not not_1 (not_1_out, floor0);
  not not_2 (not_2_out, floor1);
  not not_3 (not_3_out, floor1);
  not not_4 (not_4_out, floor_2);
  not not_5 (not_5_out, floor0);
  not not_6 (not_6_out, floor1);
  not not_7 (not_7_out, floor0);
  not not_8 (not_8_out, floor_2);
  not not_9 (not_9_out, floor1);
  not not_10 (not_10_out, floor_2);
  not not_11 (not_11_out, floor0);
  not not_12 (not_12_out, floor_2);
  not not_13 (not_13_out, floor1);
  not not_14 (not_14_out, floor_2);
  not not_15 (not_15_out, floor0);
  not not_16 (not_16_out, floor1);
  not not_17 (not_17_out, floor1);
  not not_18 (not_18_out, floor_2);
  not not_19 (not_19_out, floor0);
  not not_20 (not_20_out, floor1);
  not not_21 (not_21_out, floor1);
  not not_22 (not_22_out, floor_2);
  not not_23 (not_23_out, floor1);
  not not_24 (not_24_out, floor_2);
  not not_25 (not_25_out, floor0);
  not not_26 (not_26_out, floor1);
  and and_1 (and_1_out, not_1_out, not_2_out, floor_2);
  and and_2 (and_2_out, floor0, not_3_out, not_4_out);
  and and_3 (and_3_out, not_5_out, not_6_out, floor_2);
  and and_4 (and_4_out, not_7_out, floor1, not_8_out);
  and and_5 (and_5_out, floor0, not_9_out, not_10_out);
  and and_6 (and_6_out, not_11_out, floor1, not_12_out);
  and and_7 (and_7_out, floor0, not_13_out, not_14_out);
  and and_8 (and_8_out, not_15_out, not_16_out, floor_2);
  and and_9 (and_9_out, floor0, not_17_out, not_18_out);
  and and_10 (and_10_out, not_19_out, not_20_out, floor_2);
  and and_11 (and_11_out, floor0, not_21_out, not_22_out);
  and and_12 (f, floor0, not_23_out, not_24_out);
  and and_13 (g, not_25_out, not_26_out, floor_2);
  or or_1 (a, and_1_out, and_2_out);
  or or_2 (b, and_3_out, and_4_out, and_5_out);
  or or_3 (c, and_6_out, and_7_out);
  or or_4 (d, and_8_out, and_9_out);
  or or_5 (e, and_10_out, and_11_out);

  assign Point = 1'b1;
endmodule

module elevator (
  input  GroundRN,
  input  Floor1RN,
  input  Floor2RN,
  input  call_to_0,
  input  call_to_1,
  input  call_to_2,
  input  goto_floor,
  input  goto1,
  input  go_to_2,
  output indicate0,
  output indicate1,
  output indicate2,
  output BusyorNot,
  output Door,
  output up,
  output Down
);

  wire and_1_out, and_2_out, and_3_out, and_4_out, and_5_out, and_6_out, and_7_out, and_8_out, and_9_out,
       and_10_out, and_11_out, and_12_out, and_13_out, and_14_out, and_15_out, and_16_out, and_17_out,
       and_18_out, and_19_out, and_20_out, and_21_out, and_22_out, and_23_out, and_24_out, and_25_out,
       and_26_out, and_27_out, and_28_out, and_29_out, and_30_out, and_31_out, and_32_out, and_33_out,
       and_34_out, and_35_out, and_36_out, and_37_out, and_38_out, and_39_out, and_40_out, and_41_out,
       and_42_out, and_43_out, not_1_out, not_2_out, not_3_out, not_4_out, not_5_out, not_6_out, not_7_out,
       not_8_out, not_9_out, not_10_out, not_11_out, not_12_out, not_13_out, not_14_out, not_15_out,
       not_16_out, not_17_out, not_18_out, not_19_out, not_20_out, not_21_out, not_22_out, not_23_out,
       not_24_out, not_25_out, not_26_out, not_27_out, not_28_out, not_29_out, not_30_out, not_31_out,
       not_32_out, not_33_out, not_34_out, not_35_out, not_36_out, not_37_out, not_38_out, not_39_out,
       not_40_out, not_41_out, not_42_out;

  not not_1 (not_1_out, Floor1RN);
  not not_2 (not_2_out, Floor2RN);
  not not_3 (not_3_out, call_to_1);
  not not_4 (not_4_out, call_to_2);
  not not_5 (not_5_out, goto1);
  not not_6 (not_6_out, go_to_2);
  not not_7 (not_7_out, Floor2RN);
  not not_8 (not_8_out, Floor2RN);
  not not_9 (not_9_out, call_to_0);
  not not_10 (not_10_out, call_to_2);
  not not_11 (not_11_out, goto_floor);
  not not_12 (not_12_out, go_to_2);
  not not_13 (not_13_out, GroundRN);
  not not_14 (not_14_out, GroundRN);
  not not_15 (not_15_out, call_to_0);
  not not_16 (not_16_out, call_to_1);
  not not_17 (not_17_out, goto_floor);
  not not_18 (not_18_out, goto1);
  not not_19 (not_19_out, Floor2RN);
  not not_20 (not_20_out, Floor1RN);
  not not_21 (not_21_out, GroundRN);
  not not_22 (not_22_out, Floor2RN);
  not not_23 (not_23_out, Floor1RN);
  not not_24 (not_24_out, Floor2RN);
  not not_25 (not_25_out, Floor1RN);
  not not_26 (not_26_out, Floor1RN);
  not not_27 (not_27_out, Floor2RN);
  not not_28 (not_28_out, Floor1RN);
  not not_29 (not_29_out, Floor2RN);
  not not_30 (not_30_out, GroundRN);
  not not_31 (not_31_out, Floor2RN);
  not not_32 (not_32_out, call_to_0);
  not not_33 (not_33_out, call_to_1);
  not not_34 (not_34_out, goto_floor);
  not not_35 (not_35_out, goto1);
  not not_36 (not_36_out, Floor1RN);
  not not_37 (not_37_out, Floor2RN);
  not not_38 (not_38_out, Floor1RN);
  not not_39 (not_39_out, Floor2RN);
  not not_40 (not_40_out, GroundRN);
  not not_41 (not_41_out, call_to_2);
  not not_42 (not_42_out, go_to_2);
  and and_1 (and_1_out, not_1_out, not_2_out, not_3_out, not_4_out, not_5_out, not_6_out);
  and and_2 (and_2_out, not_7_out, goto_floor);
  and and_3 (and_3_out, not_8_out, call_to_0);
  and and_4 (and_4_out, Floor2RN, goto_floor);
  and and_5 (and_5_out, Floor2RN, call_to_0);
  and and_6 (and_6_out, Floor1RN, not_9_out, not_10_out, not_11_out, not_12_out);
  and and_7 (and_7_out, GroundRN, go_to_2);
  and and_8 (and_8_out, GroundRN, call_to_2);
  and and_9 (and_9_out, not_13_out, go_to_2);
  and and_10 (and_10_out, not_14_out, call_to_2);
  and and_11 (and_11_out, Floor2RN, not_15_out, not_16_out, not_17_out, not_18_out);
  and and_12 (and_12_out, not_19_out, go_to_2);
  and and_13 (and_13_out, not_20_out, goto1);
  and and_14 (and_14_out, not_21_out, goto_floor);
  and and_15 (and_15_out, not_22_out, call_to_2);
  and and_16 (and_16_out, not_23_out, call_to_1);
  and and_17 (and_17_out, Floor2RN, call_to_0);
  and and_18 (and_18_out, Floor1RN, call_to_0);
  and and_19 (and_19_out, not_24_out, go_to_2);
  and and_20 (and_20_out, not_25_out, goto1);
  and and_21 (and_21_out, not_26_out, call_to_1);
  and and_22 (and_22_out, Floor2RN, goto_floor);
  and and_23 (and_23_out, Floor2RN, call_to_0);
  and and_24 (and_24_out, Floor1RN, goto_floor);
  and and_25 (and_25_out, Floor1RN, call_to_2);
  and and_26 (and_26_out, Floor1RN, call_to_0);
  and and_27 (and_27_out, GroundRN, call_to_2);
  and and_28 (and_28_out, not_27_out, go_to_2);
  and and_29 (and_29_out, not_28_out, not_29_out, goto1);
  and and_30 (and_30_out, not_30_out, not_31_out, not_32_out, not_33_out, call_to_2, not_34_out, not_35_out);
  and and_31 (and_31_out, not_36_out, not_37_out, call_to_2);
  and and_32 (and_32_out, not_38_out, not_39_out, call_to_1);
  and and_33 (and_33_out, Floor2RN, goto1);
  and and_34 (and_34_out, not_40_out, Floor2RN, not_41_out, goto_floor, not_42_out);
  and and_35 (and_35_out, Floor2RN, call_to_1);
  and and_36 (and_36_out, Floor2RN, call_to_0);
  and and_37 (and_37_out, Floor1RN, goto_floor);
  and and_38 (and_38_out, Floor1RN, call_to_2, go_to_2);
  and and_39 (and_39_out, Floor1RN, call_to_2, goto1);
  and and_40 (and_40_out, Floor1RN, call_to_1, call_to_2);
  and and_41 (and_41_out, Floor1RN, call_to_0);
  and and_42 (and_42_out, Floor1RN, Floor2RN, call_to_2);
  and and_43 (and_43_out, GroundRN, Floor1RN, call_to_2);
  or or_1 (indicate0, and_1_out, and_2_out, and_3_out);
  or or_2 (indicate1, goto1, call_to_1, and_4_out, and_5_out, and_6_out, and_7_out, and_8_out);
  or or_3 (indicate2, and_9_out, and_10_out, and_11_out);
  or or_4 (BusyorNot, and_12_out, and_13_out, and_14_out, and_15_out, and_16_out, and_17_out, and_18_out);
  or or_5 (Door, and_19_out, and_20_out, and_21_out, and_22_out, and_23_out, and_24_out, and_25_out, and_26_out, and_27_out);
  or or_6 (up, and_28_out, and_29_out, and_30_out, and_31_out, and_32_out);
  or or_7 (Down, and_33_out, and_34_out, and_35_out, and_36_out, and_37_out, and_38_out, and_39_out, and_40_out, and_41_out, and_42_out, and_43_out);
endmodule

module Floor_Buttons (
  input  Go2,
  input  Go1,
  input  Go0,
  input  Call2,
  input  Call1,
  input  Call0,
  output go2out,
  output go1out,
  output go0out,
  output call2out,
  output call1out,
  output call0out
);

  wire clock_1_out;

  Clock clock_1 (.out(clock_1_out));
  D_Flip_Flop go2ff (.Q(go2out), .preset(Go2), .reset(clock_1_out));  // open: clk, D, Qn, en
  D_Flip_Flop go1ff (.Q(go1out), .preset(Go1), .reset(clock_1_out));  // open: clk, D, Qn, en
  D_Flip_Flop go0ff (.Q(go0out), .preset(Go0), .reset(clock_1_out));  // open: clk, D, Qn, en
  D_Flip_Flop call2ff (.Q(call2out), .preset(Call2), .reset(clock_1_out));  // open: clk, D, Qn, en
  D_Flip_Flop call1ff (.Q(call1out), .preset(Call1), .reset(clock_1_out));  // open: clk, D, Qn, en
  D_Flip_Flop call0ff (.Q(call0out), .preset(Call0), .reset(clock_1_out));  // open: clk, D, Qn, en
endmodule

module ButtonsWAlarm (
  input  Go2,
  input  Go1,
  input  Go0,
  input  Call2,
  input  Call1,
  input  Call0,
  input  Alarm_ON,
  input  Alarm_OFF,
  output go2t,
  output go1t,
  output go0t,
  output call2t,
  output call1t,
  output call0t,
  output Alarm_LED
);

  wire call0ff_q, call1ff_q, call2ff_q, clock_1_out, d_ff_1_qn, go0ff_q, go1ff_q, go2ff_q;

  D_Flip_Flop go2ff (.Q(go2ff_q), .preset(Go2), .reset(clock_1_out));  // open: clk, D, Qn, en
  D_Flip_Flop go1ff (.Q(go1ff_q), .preset(Go1), .reset(clock_1_out));  // open: clk, D, Qn, en
  D_Flip_Flop go0ff (.Q(go0ff_q), .preset(Go0), .reset(clock_1_out));  // open: clk, D, Qn, en
  Clock clock_1 (.out(clock_1_out));
  D_Flip_Flop call2ff (.Q(call2ff_q), .preset(Call2), .reset(clock_1_out));  // open: clk, D, Qn, en
  D_Flip_Flop d_ff_1 (.Q(Alarm_LED), .Qn(d_ff_1_qn), .preset(Alarm_ON), .reset(Alarm_OFF));  // open: clk, D, en
  D_Flip_Flop call1ff (.Q(call1ff_q), .preset(Call1), .reset(clock_1_out));  // open: clk, D, Qn, en
  D_Flip_Flop call0ff (.Q(call0ff_q), .preset(Call0), .reset(clock_1_out));  // open: clk, D, Qn, en
  and and_1 (go2t, d_ff_1_qn, go2ff_q);
  and and_2 (go1t, d_ff_1_qn, go1ff_q);
  and and_3 (go0t, go0ff_q, go0ff_q, d_ff_1_qn);
  and and_4 (call2t, d_ff_1_qn, call2ff_q);
  and and_5 (call1t, d_ff_1_qn, call1ff_q);
  and and_6 (call0t, call0ff_q, d_ff_1_qn);
endmodule
